// Logisim project CPU.circ as structural Verilog: 1 circuit, main circuit main
module main (
  output [1:0] WriteReg,
  output [1:0] ReadReg1,
  output [1:0] ReadReg2,
  output [7:0] out_4,
  output [7:0] out_5
);

  wire and_1_out, and_2_out, and_3_out, and_4_out, and_5_out, button_1_out, decoder_1_out0, decoder_1_out1,
       decoder_1_out2, decoder_1_out3, not_1_out, not_2_out, or_1_out, TheClock_out;
  wire [1:0] InstructionMemory_dout_2;
  wire [3:0] multiplexer_3_out, multiplexer_3_out_2, multiplexer_4_out, multiplexer_4_out_2, PC_q, PC_q_2;
  wire [7:0] adder_1_out, adder_2_out, MainMemory_dout, R0_q, R1_q, R2_q, R3_q, subtractor_1_out;
  wire [7:6] InstructionMemory_dout;

  and and_1 (and_1_out, InstructionMemory_dout[6], InstructionMemory_dout[7]);
  not not_1 (not_1_out, or_1_out);
  LED Tic (.in(not_1_out));
  LED MemWrite (.in(and_1_out));
  Clock TheClock (.out(TheClock_out));
  Button button_1 (.out(button_1_out));
  LED Toc (.in(or_1_out));
  not not_2 (not_2_out, and_1_out);
  Decoder #(.select(2)) decoder_1 (
    .out0(decoder_1_out0), .out1(decoder_1_out1), .out2(decoder_1_out2), .out3(decoder_1_out3), .sel(WriteReg));  // open: en
  or or_1 (or_1_out, TheClock_out, button_1_out);
  Register PC (.D(adder_2_out), .en(1'b1), .clk(or_1_out), .Q({PC_q_2, PC_q}));  // open: clr
  RAM #(.enables("line")) InstructionMemory (
    .addr({PC_q_2, PC_q}), .clk(or_1_out),
    .dout({InstructionMemory_dout, WriteReg, InstructionMemory_dout_2, ReadReg2}));  // open: we, din
  LED WriteEnable (.in(not_2_out));
  Adder adder_1 (
    .a({multiplexer_3_out_2, multiplexer_3_out}), .b({multiplexer_4_out_2, multiplexer_4_out}),
    .out(adder_1_out));  // open: cin, cout
  Subtractor subtractor_1 (
    .a({multiplexer_3_out_2, multiplexer_3_out}), .b({multiplexer_4_out_2, multiplexer_4_out}),
    .out(subtractor_1_out));  // open: bin, bout
  Adder adder_2 (.a({PC_q_2, PC_q}), .b(8'h1), .out(adder_2_out));  // open: cin, cout
  Multiplexer #(.width(8)) multiplexer_1 (
    .in0(adder_1_out), .in1(subtractor_1_out), .out(out_4), .sel(InstructionMemory_dout[6]));
  RAM #(.addrWidth(4), .enables("line")) MainMemory (
    .addr({InstructionMemory_dout_2, ReadReg2}), .we(and_1_out), .clk(or_1_out),
    .din({multiplexer_3_out_2, multiplexer_3_out}), .dout(MainMemory_dout));
  Hex_Digit_Display Address (.value({InstructionMemory_dout_2, ReadReg2}));  // open: dp
  Hex_Digit_Display hex_digit_display_1 (.value(PC_q_2));  // open: dp
  and and_2 (and_2_out, decoder_1_out0, not_2_out);
  and and_3 (and_3_out, decoder_1_out1, not_2_out);
  and and_4 (and_4_out, decoder_1_out2, not_2_out);
  and and_5 (and_5_out, decoder_1_out3, not_2_out);
  Multiplexer #(.width(8)) multiplexer_2 (
    .in0(out_4), .in1(MainMemory_dout), .out(out_5), .sel(InstructionMemory_dout[7]));
  Hex_Digit_Display PCDisplay (.value(PC_q));  // open: dp
  Hex_Digit_Display hex_digit_display_2 (.value({InstructionMemory_dout, WriteReg}));  // open: dp
  LED led_1 (.in(and_2_out));
  LED led_2 (.in(and_3_out));
  LED led_3 (.in(and_4_out));
  LED led_4 (.in(and_5_out));
  Hex_Digit_Display Instruction (.value({InstructionMemory_dout_2, ReadReg2}));  // open: dp
  Register R0 (.D(out_5), .en(and_2_out), .clk(or_1_out), .Q(R0_q));  // open: clr
  Register R1 (.D(out_5), .en(and_3_out), .clk(or_1_out), .Q(R1_q));  // open: clr
  Register R2 (.D(out_5), .en(and_4_out), .clk(or_1_out), .Q(R2_q));  // open: clr
  Register R3 (.D(out_5), .en(and_5_out), .clk(or_1_out), .Q(R3_q));  // open: clr
  Hex_Digit_Display DRAM (.value(MainMemory_dout[7:4]));  // open: dp
  Hex_Digit_Display Data (.value(MainMemory_dout[3:0]));  // open: dp
  Hex_Digit_Display Register0 (.value(R0_q[7:4]));  // open: dp
  Hex_Digit_Display hex_digit_display_3 (.value(R0_q[3:0]));  // open: dp
  Hex_Digit_Display Register1 (.value(R1_q[7:4]));  // open: dp
  Multiplexer #(.select(2), .width(8)) multiplexer_3 (
    .in0(R0_q), .in1(R1_q), .in2(R2_q), .in3(R3_q), .out({multiplexer_3_out_2, multiplexer_3_out}),
    .sel(ReadReg1));
  Multiplexer #(.select(2), .width(8)) multiplexer_4 (
    .in0(R0_q), .in1(R1_q), .in2(R2_q), .in3(R3_q), .out({multiplexer_4_out_2, multiplexer_4_out}),
    .sel(ReadReg2));
  Hex_Digit_Display hex_digit_display_4 (.value(R1_q[3:0]));  // open: dp
  Hex_Digit_Display Register2 (.value(R2_q[7:4]));  // open: dp
  Multiplexer #(.width(2)) multiplexer_5 (
    .in0(InstructionMemory_dout_2), .in1(WriteReg), .out(ReadReg1), .sel(InstructionMemory_dout[7]));
  Hex_Digit_Display hex_digit_display_5 (.value(R2_q[3:0]));  // open: dp
  Hex_Digit_Display RegData1 (.value(multiplexer_3_out_2));  // open: dp
  Hex_Digit_Display Register3 (.value(R3_q[7:4]));  // open: dp
  Hex_Digit_Display hex_digit_display_6 (.value(R3_q[3:0]));  // open: dp
  Hex_Digit_Display hex_digit_display_7 (.value(multiplexer_3_out));  // open: dp
  Hex_Digit_Display RegData2 (.value(multiplexer_4_out_2));  // open: dp
  Hex_Digit_Display hex_digit_display_8 (.value(multiplexer_4_out));  // open: dp

  // Notes on the sheet:
  //   Opcode Bits
  //   Vedhesh Anandhan Kamaraj
  //   Dhruv Mittal
  //   I pledge my honor that I have abided by the Stevens Honor System.
endmodule
